# Fritzing sketch pcboard (saved by Fritzing 0.8.7b)
circuit board: 10.16cm x 5.36194cm
breadboards: 1

parts:
  Componente1 = Arduino Mega 2560 (Rev3)
  WATERTEMP = TMP36 Temperature Sensor [package="TO92 [THT]"]
  RELAY = Toggle Switch [package=THT]
  EXTTEMP = Toggle Switch [package=THT]
  R1 = Resistor [tolerance=±5% resistance=4.7k package=THT]
  LEDBOARD = Header 5x2 [package=2x5-shrouded_smd]

nets:
  GND: Componente1.GND, WATERTEMP.GND, RELAY.L1, EXTTEMP.L2, LEDBOARD.2
  N1: Componente1.D13_PWM, RELAY.L2
  N2: Componente1.5V, WATERTEMP.+Vs, RELAY.COM, EXTTEMP.L1, R1.Pin_0, LEDBOARD.1
  N3: Componente1.D2_PWM, LEDBOARD.3
  N4: Componente1.D3_PWM, LEDBOARD.4
  N5: Componente1.D4_PWM, LEDBOARD.5
  N6: Componente1.D6_PWM, EXTTEMP.COM
  N7: Componente1.D7_PWM, WATERTEMP.Vout, R1.Pin_1
